# Fritzing sketch miniTimeControl (saved by Fritzing 0.9.4)
breadboards: 1

parts:
  Teensy4_0 = Teensy 4.0
  LED1 = smd LED [color="Red (633nm)" package="1206 [SMD]"]
  LED2 = smd LED [color="Yellow (595nm)" package="1206 [SMD]"]
  LED3 = smd LED [color="Green (570nm)" package="1206 [SMD]"]
  R1 = Resistor [tolerance=±5% resistance=100 package="0402 [SMD]"]
  R2 = Resistor [tolerance=±5% resistance=100 package="0402 [SMD]"]
  R3 = Resistor [tolerance=±5% resistance=100 package="0402 [SMD]"]
  Buzzer = Buzzer 12mm [package=buzzer-12mm]
  ON/OFF_button = SWITCH-MOMENTARY-2 [package=tactile-pth-12mm]

nets:
  N1: Teensy4_0.pin_1, Teensy4_0.pin_32, LED1.cathode, LED2.cathode, LED3.cathode, Buzzer.1, ON/OFF_button.1
  N2: Teensy4_0.pin_5, Buzzer.2
  N3: Teensy4_0.pin_7, R1.Pin_0
  N4: Teensy4_0.pin_9, R3.Pin_0
  N5: Teensy4_0.pin_11, R2.Pin_0
  N6: Teensy4_0.pin_19, ON/OFF_button.2
  N7: LED1.anode, R2.Pin_1
  N8: LED2.anode, R3.Pin_1
  N9: LED3.anode, R1.Pin_1

custom parts:
  Teensy 4.0: The Teensy is a complete USB-based microcontoller development system, in a very small footprint, capable of implementing many types of projects. All programming is done via the USB port. No special programmer is needed, only a standard micro-USB cable and a PC or Macintosh with a USB port.
